# Fritzing sketch HCSR04P (saved by Fritzing 0.9.3b)

parts:
  Raspberry_Pi_1 = Raspberry Pi 3 [part_number=RPI-3-V1.2]
  Part1 = SRF05 Ultrasonic Rangefinder

nets:
  3V3: Raspberry_Pi_1.3v3, Part1.VCC
  N1: Raspberry_Pi_1.GPIO17, Part1.Trig
  N2: Raspberry_Pi_1.GPIO27, Part1.Echo
  GND: Raspberry_Pi_1.GND, Part1.GND
